// Logisim project dlatch_tictactoc.circ as structural Verilog
module D_latch (
  input  D,
  input  Enable,
  output Q,
  output notQ
);

  wire and_1_out, and_2_out, not_1_out;

  not not_1 (not_1_out, D);
  and and_1 (and_1_out, not_1_out, Enable);
  and and_2 (and_2_out, Enable, D);
  nor nor_1 (Q, and_1_out, notQ);
  nor nor_2 (notQ, Q, and_2_out);
endmodule

module playerswitch (
  input  key,
  input  switch,
  output player1,
  output player2
);

  wire and_1_out, d_latch_1_q, xnor_1_out;

  and and_1 (and_1_out, key, xnor_1_out);
  Demultiplexer demultiplexer_1 (.out0(player1), .out1(player2), .in(key), .sel(d_latch_1_q));
  D_latch d_latch_1 (.D(switch), .Enable(and_1_out), .Q(d_latch_1_q));  // open: notQ
  xnor xnor_1 (xnor_1_out, player1, player2);
endmodule

module D_latch_lock (
  input  D,
  input  WE,
  output Q
);

  wire d_latch_1_q, or_1_out;

  or or_1 (or_1_out, D, WE);
  not not_1 (Q, d_latch_1_q);
  D_latch d_latch_1 (.D(D), .Enable(or_1_out), .Q(d_latch_1_q));  // open: notQ
endmodule

module D_latch_lock_2 (
  input  D,
  input  WE,
  output Q
);

  wire or_1_out;

  or or_1 (or_1_out, D, WE);
  D_latch d_latch_1 (.D(D), .Enable(or_1_out), .Q(Q));  // open: notQ
endmodule

module RGB_selector (
  input  p1,
  input  p2,
  output [7:0] out_3,
  output [7:0] out_4
);

  Multiplexer #(.width(8)) multiplexer_1 (.in0({8{1'b0}}), .in1({8{1'b1}}), .out(out_3), .sel(p1));
  Multiplexer #(.width(8)) multiplexer_2 (.in0({8{1'b0}}), .in1({8{1'b1}}), .out(out_4), .sel(p2));
endmodule

module Inputmemory (
  input  d_able,
  input  k_9,
  input  k_8,
  input  k_7,
  input  k_6,
  input  k_5,
  input  k_4,
  input  k_3,
  input  k_2,
  input  k_1,
  input  reset,
  output A9,
  output A8,
  output A7,
  output A6,
  output A5,
  output A4,
  output A3,
  output A2,
  output A1,
  output B9,
  output B8,
  output B7,
  output B6,
  output B5,
  output B4,
  output B3,
  output B2,
  output B1,
  output Astate
);

  wire and_1_out, and_2_out, and_3_out, and_4_out, and_5_out, and_6_out, and_7_out, and_8_out, and_9_out,
       bitcounter_1_1_value, d_latch_lock_2_1_q, d_latch_lock_2_2_q, d_latch_lock_2_3_q, d_latch_lock_2_4_q,
       d_latch_lock_2_5_q, d_latch_lock_2_6_q, d_latch_lock_2_7_q, d_latch_lock_2_8_q, d_latch_lock_2_9_q,
       or_1_out, playerswitch_1_player1, playerswitch_1_player2, playerswitch_2_player1,
       playerswitch_2_player2, playerswitch_3_player1, playerswitch_3_player2, playerswitch_4_player1,
       playerswitch_4_player2, playerswitch_5_player1, playerswitch_5_player2, playerswitch_6_player1,
       playerswitch_6_player2, playerswitch_7_player1, playerswitch_7_player2, playerswitch_8_player1,
       playerswitch_8_player2, playerswitch_9_player1, playerswitch_9_player2, xnor_1_out;

  D_latch_lock_2 d_latch_lock_2_1 (.D(k_9), .WE(reset), .Q(d_latch_lock_2_1_q));
  D_latch_lock_2 d_latch_lock_2_2 (.D(k_8), .WE(reset), .Q(d_latch_lock_2_2_q));
  D_latch_lock_2 d_latch_lock_2_3 (.D(k_7), .WE(reset), .Q(d_latch_lock_2_3_q));
  D_latch_lock_2 d_latch_lock_2_4 (.D(k_6), .WE(reset), .Q(d_latch_lock_2_4_q));
  D_latch_lock_2 d_latch_lock_2_5 (.D(k_5), .WE(reset), .Q(d_latch_lock_2_5_q));
  D_latch_lock_2 d_latch_lock_2_6 (.D(k_4), .WE(reset), .Q(d_latch_lock_2_6_q));
  D_latch_lock_2 d_latch_lock_2_7 (.D(k_3), .WE(reset), .Q(d_latch_lock_2_7_q));
  D_latch_lock_2 d_latch_lock_2_8 (.D(k_2), .WE(reset), .Q(d_latch_lock_2_8_q));
  D_latch_lock_2 d_latch_lock_2_9 (.D(k_1), .WE(reset), .Q(d_latch_lock_2_9_q));
  xnor xnor_1 (xnor_1_out, d_able, reset);
  and and_1 (and_1_out, ~d_latch_lock_2_1_q, k_9);  // AND_Gate
  and and_2 (and_2_out, ~d_latch_lock_2_2_q, k_8);  // AND_Gate
  and and_3 (and_3_out, ~d_latch_lock_2_3_q, k_7);  // AND_Gate
  and and_4 (and_4_out, ~d_latch_lock_2_4_q, k_6);  // AND_Gate
  and and_5 (and_5_out, ~d_latch_lock_2_5_q, k_5);  // AND_Gate
  and and_6 (and_6_out, ~d_latch_lock_2_6_q, k_4);  // AND_Gate
  and and_7 (and_7_out, ~d_latch_lock_2_7_q, k_3);  // AND_Gate
  and and_8 (and_8_out, ~d_latch_lock_2_8_q, k_2);  // AND_Gate
  and and_9 (and_9_out, ~d_latch_lock_2_9_q, k_1);  // AND_Gate
  playerswitch playerswitch_1 (
    .key(d_latch_lock_2_1_q), .switch(bitcounter_1_1_value), .player1(playerswitch_1_player1),
    .player2(playerswitch_1_player2));
  playerswitch playerswitch_2 (
    .key(d_latch_lock_2_2_q), .switch(bitcounter_1_1_value), .player1(playerswitch_2_player1),
    .player2(playerswitch_2_player2));
  playerswitch playerswitch_3 (
    .key(d_latch_lock_2_3_q), .switch(bitcounter_1_1_value), .player1(playerswitch_3_player1),
    .player2(playerswitch_3_player2));
  playerswitch playerswitch_4 (
    .key(d_latch_lock_2_4_q), .switch(bitcounter_1_1_value), .player1(playerswitch_4_player1),
    .player2(playerswitch_4_player2));
  playerswitch playerswitch_5 (
    .key(d_latch_lock_2_5_q), .switch(bitcounter_1_1_value), .player1(playerswitch_5_player1),
    .player2(playerswitch_5_player2));
  playerswitch playerswitch_6 (
    .key(d_latch_lock_2_6_q), .switch(bitcounter_1_1_value), .player1(playerswitch_6_player1),
    .player2(playerswitch_6_player2));
  playerswitch playerswitch_7 (
    .key(d_latch_lock_2_7_q), .switch(bitcounter_1_1_value), .player1(playerswitch_7_player1),
    .player2(playerswitch_7_player2));
  playerswitch playerswitch_8 (
    .key(d_latch_lock_2_8_q), .switch(bitcounter_1_1_value), .player1(playerswitch_8_player1),
    .player2(playerswitch_8_player2));
  playerswitch playerswitch_9 (
    .key(d_latch_lock_2_9_q), .switch(bitcounter_1_1_value), .player1(playerswitch_9_player1),
    .player2(playerswitch_9_player2));
  or or_1 (or_1_out, and_1_out, and_2_out, and_3_out, and_4_out, and_5_out, and_6_out, and_7_out, and_8_out, and_9_out);
  bitcounter_1 bitcounter_1_1 (
    .maxvalue(1'b1), .clock(or_1_out), .reset(reset), .value(bitcounter_1_1_value));  // open: zero
  D_latch d_latch_1 (.D(playerswitch_1_player1), .Enable(xnor_1_out), .Q(A9));  // open: notQ
  D_latch d_latch_2 (.D(playerswitch_1_player2), .Enable(xnor_1_out), .Q(B9));  // open: notQ
  D_latch d_latch_3 (.D(playerswitch_2_player2), .Enable(xnor_1_out), .Q(B8));  // open: notQ
  D_latch d_latch_4 (.D(playerswitch_3_player2), .Enable(xnor_1_out), .Q(B7));  // open: notQ
  D_latch d_latch_5 (.D(playerswitch_4_player2), .Enable(xnor_1_out), .Q(B6));  // open: notQ
  D_latch d_latch_6 (.D(playerswitch_5_player2), .Enable(xnor_1_out), .Q(B5));  // open: notQ
  D_latch d_latch_7 (.D(playerswitch_6_player2), .Enable(xnor_1_out), .Q(B4));  // open: notQ
  D_latch d_latch_8 (.D(playerswitch_7_player2), .Enable(xnor_1_out), .Q(B3));  // open: notQ
  D_latch d_latch_9 (.D(playerswitch_8_player2), .Enable(xnor_1_out), .Q(B2));  // open: notQ
  D_latch d_latch_10 (.D(playerswitch_9_player2), .Enable(xnor_1_out), .Q(B1));  // open: notQ
  D_latch d_latch_11 (.D(playerswitch_2_player1), .Enable(xnor_1_out), .Q(A8));  // open: notQ
  D_latch d_latch_12 (.D(playerswitch_3_player1), .Enable(xnor_1_out), .Q(A7));  // open: notQ
  D_latch d_latch_13 (.D(playerswitch_4_player1), .Enable(xnor_1_out), .Q(A6));  // open: notQ
  D_latch d_latch_14 (.D(playerswitch_5_player1), .Enable(xnor_1_out), .Q(A5));  // open: notQ
  D_latch d_latch_15 (.D(playerswitch_6_player1), .Enable(xnor_1_out), .Q(A4));  // open: notQ
  D_latch d_latch_16 (.D(playerswitch_7_player1), .Enable(xnor_1_out), .Q(A3));  // open: notQ
  D_latch d_latch_17 (.D(playerswitch_8_player1), .Enable(xnor_1_out), .Q(A2));  // open: notQ
  D_latch d_latch_18 (.D(playerswitch_9_player1), .Enable(xnor_1_out), .Q(A1));  // open: notQ
  D_latch d_latch_19 (.D(bitcounter_1_1_value), .Enable(xnor_1_out), .Q(Astate));  // open: notQ
endmodule

module bitcounter_1 (
  input  maxvalue,
  input  clock,
  input  reset,
  output value,
  output zero
);

  Counter #(.max('h1), .width(1)) counter_1 (
    .D(maxvalue), .count(1'b1), .Q(value), .carry(zero), .up(1'b1), .clk(clock), .clr(reset));  // open: load
endmodule

module win_calc (
  input  in_1,
  input  in_2,
  input  in_3,
  input  in_4,
  input  in_5,
  input  in_6,
  input  in_7,
  input  in_8,
  input  in_9,
  output Win
);

  wire A123_out, A147_out, A159_out, A258_out, A357_out, A369_out, A456_out, A789_out;

  and A123 (A123_out, in_1, in_2, in_3);
  and A456 (A456_out, in_4, in_5, in_6);
  and A789 (A789_out, in_7, in_8, in_9);
  and A147 (A147_out, in_1, in_4, in_7);
  and A258 (A258_out, in_2, in_5, in_8);
  and A369 (A369_out, in_3, in_6, in_9);
  and A159 (A159_out, in_1, in_5, in_9);
  and A357 (A357_out, in_3, in_5, in_7);
  or or_1 (Win, A123_out, A456_out, A789_out, A147_out, A258_out, A369_out, A159_out, A357_out);
endmodule
